# Fritzing sketch Co2 (saved by Fritzing 0.9.4)
breadboards: 1

parts:
  Componente1 = Arduino Nano (Rev3.0)
  U1 = Nokia 6100 Color LCD [package=nokia6100_lcd]
  Componente2 = Gas Sensor Breakout Board
  J1 = Piezo Speaker
  RHT1 = Humidity and Temperature Sensor RHT03
  R1 = Resistor [tolerance=±5% resistance=4.7k package="2512 [SMD]"]
  LED1 = RGB LED (com. cathode, rgb) [package="5 mm [THT]"]  # not connected
  Componente3 = Barometric Pressure Sensor - BMP180 Breakout (GY-68)

nets:
  GND: Componente1.GND, Componente2.GND, J1.pin1, RHT1.GND_2, Componente3.GND
  N1: Componente1.D2, RHT1.Data-signal, R1.Pin_0
  N2: Componente1.D4, J1.pin2
  N3: Componente1.D7, U1.CS
  N4: Componente1.D8, U1.SCK
  N5: Componente1.D11/MOSI, U1.LEDGND
  5V: Componente1.5V, Componente2.B1, RHT1.Vcc, R1.Pin_1
  N6: Componente1.A5, Componente3.SCL
  N7: Componente1.A4, Componente3.SDA
  N8: Componente1.A0, Componente2.A1
  3V3: Componente1.3V3, U1.VDISPLAY, Componente3.VCC
  N9: Componente1.D13/SCK, U1.GND
